// Logisim project completed_ITC_CPU.circ as structural Verilog: 34 circuits, main circuit main
module main (
  input  Clock,
  input  WE,
  input  Din,
  input  Oe,
  input  Reset,
  output out_6,
  output out_7
);

  wire and_1_out, and_2_out, not_1_out, or_1_out;

  not not_1 (not_1_out, WE);
  and and_1 (and_1_out, out_7, not_1_out);
  and and_2 (and_2_out, WE, Din);
  or or_1 (or_1_out, and_1_out, and_2_out);
  D_Flip_Flop d_ff_1 (.D(or_1_out), .clk(Clock), .Q(out_7), .preset(Reset));  // open: Qn, reset
  assign out_6 = Oe ? out_7 : 1'bz;  // Controlled_Buffer controlled_buffer_1
endmodule

module OneBitAdder (
  input  A,
  input  B,
  input  CarryIn,
  output Sum,
  output CarryOut
);

  wire and_1_out, and_2_out, xor_1_out;

  xor xor_1 (xor_1_out, A, B);
  and and_1 (and_1_out, A, B);
  and and_2 (and_2_out, xor_1_out, CarryIn);
  xor xor_2 (Sum, CarryIn, xor_1_out);
  or or_1 (CarryOut, and_2_out, and_1_out);
  LED led_1 (.in(Sum));
  LED led_2 (.in(CarryOut));

  // Notes on the sheet:
  //   Intermediate Sum
  //   Intermediate Carry
endmodule

module FourBitAdder (
  input  CarryIn,
  input  [3:0] A,
  input  [3:0] B,
  output [3:0] Sum,
  output CarryOut
);

  wire onebitadder_1_carryout, onebitadder_2_carryout, onebitadder_3_carryout;

  // Probe on A
  // Probe on B
  OneBitAdder onebitadder_1 (.A(A[0]), .B(B[0]), .CarryIn(CarryIn), .Sum(Sum[0]), .CarryOut(onebitadder_1_carryout));
  OneBitAdder onebitadder_2 (
    .A(A[1]), .B(B[1]), .CarryIn(onebitadder_1_carryout), .Sum(Sum[1]), .CarryOut(onebitadder_2_carryout));
  OneBitAdder onebitadder_3 (
    .A(A[2]), .B(B[2]), .CarryIn(onebitadder_2_carryout), .Sum(Sum[2]), .CarryOut(onebitadder_3_carryout));
  OneBitAdder onebitadder_4 (.A(A[3]), .B(B[3]), .CarryIn(onebitadder_3_carryout), .Sum(Sum[3]), .CarryOut(CarryOut));
  // Probe on Sum

  // Notes on the sheet:
  //   First
  //   Second
  //   Third
  //   Fourth
endmodule

module EightBitAdder (
  input  CarryIn,
  input  [7:0] A,
  input  [7:0] B,
  output [7:0] Sum,
  output CarryOut
);

  wire fourbitadder_1_carryout;

  // Probe on A
  // Probe on B
  FourBitAdder fourbitadder_1 (
    .CarryIn(CarryIn), .A(A[3:0]), .B(B[3:0]), .Sum(Sum[3:0]), .CarryOut(fourbitadder_1_carryout));
  FourBitAdder fourbitadder_2 (
    .CarryIn(fourbitadder_1_carryout), .A(A[7:4]), .B(B[7:4]), .Sum(Sum[7:4]), .CarryOut(CarryOut));
  // Probe on Sum

  // Notes on the sheet:
  //   First
  //   Second 
endmodule

module SixteenBitAdder (
  input  CarryIn,
  input  [15:0] A,
  input  [15:0] B,
  output [15:0] Sum,
  output CarryOut
);

  wire eightbitadder_1_carryout;

  // Probe on A
  // Probe on B
  EightBitAdder eightbitadder_1 (
    .CarryIn(CarryIn), .A(A[7:0]), .B(B[7:0]), .Sum(Sum[7:0]), .CarryOut(eightbitadder_1_carryout));
  EightBitAdder eightbitadder_2 (
    .CarryIn(eightbitadder_1_carryout), .A(A[15:8]), .B(B[15:8]), .Sum(Sum[15:8]), .CarryOut(CarryOut));
  // Probe on Sum

  // Notes on the sheet:
  //   First
  //   Second 
endmodule

module SixteenBitAdd_Sub (
  input  CarryIn,
  input  [15:0] A,
  input  [15:0] B,
  input  [15:0] Sub,
  output [15:0] Result,
  output CarryOut
);

  wire [15:0] xor_1_out;

  // Probe on Sub
  // Probe on A
  // Probe on B
  assign xor_1_out = B ^ Sub;  // XOR_Gate xor_1, 16 bits wide
  SixteenBitAdder sixteenbitadder_1 (.CarryIn(CarryIn), .A(A), .B(xor_1_out), .Sum(Result), .CarryOut(CarryOut));
  // Probe on Result
endmodule

module Memory_Cell (
  input  clock,
  input  WE,
  input  Din,
  input  OE,
  input  Reset,
  output Dout,
  output Stored_Data
);

  wire and_1_out, and_2_out, not_1_out, or_1_out;

  not not_1 (not_1_out, WE);
  and and_1 (and_1_out, Stored_Data, not_1_out);
  and and_2 (and_2_out, WE, Din);
  or or_1 (or_1_out, and_1_out, and_2_out);
  D_Flip_Flop d_ff_1 (.D(or_1_out), .clk(clock), .Q(Stored_Data), .reset(Reset));  // open: Qn, preset
  assign Dout = OE ? Stored_Data : 1'bz;  // Controlled_Buffer controlled_buffer_1

  // Notes on the sheet:
  //   Memory Cell
endmodule

module fourBitMulti (
  input  [3:0] B,
  input  [3:0] A,
  output [7:0] Product
);

  wire [2:0] and_15_out;
  wire [3:0] and_4_out, and_8_out, and_12_out, fourbitadder_2_carryout;
  wire [3:1] fourbitadder_3_sum;
  wire [3:3] fourbitadder_3_carryout;

  // Probe on B
  and and_1 (and_4_out[3], B[3], A[3]);
  and and_2 (and_4_out[2], B[3], A[2]);
  and and_3 (and_4_out[1], B[3], A[1]);
  and and_4 (and_4_out[0], B[3], A[0]);
  and and_5 (and_8_out[3], B[2], A[3]);
  and and_6 (and_8_out[2], B[2], A[2]);
  and and_7 (and_8_out[1], B[2], A[1]);
  and and_8 (and_8_out[0], B[2], A[0]);
  and and_9 (and_12_out[3], B[1], A[3]);
  and and_10 (and_12_out[2], B[1], A[2]);
  and and_11 (and_12_out[1], B[1], A[1]);
  and and_12 (and_12_out[0], B[1], A[0]);
  FourBitAdder fourbitadder_1 (
    .CarryIn(1'b0), .A(fourbitadder_2_carryout), .B(and_4_out), .Sum(Product[6:3]), .CarryOut(Product[7]));
  FourBitAdder fourbitadder_2 (
    .CarryIn(1'b0), .A({fourbitadder_3_carryout[3], fourbitadder_3_sum}), .B(and_8_out),
    .Sum({fourbitadder_2_carryout[2:0], Product[2]}), .CarryOut(fourbitadder_2_carryout[3]));
  and and_13 (and_15_out[2], B[0], A[3]);
  and and_14 (and_15_out[1], B[0], A[2]);
  and and_15 (and_15_out[0], B[0], A[1]);
  FourBitAdder fourbitadder_3 (
    .CarryIn(1'b0), .A({1'b0, and_15_out}), .B(and_12_out), .Sum({fourbitadder_3_sum, Product[1]}),
    .CarryOut(fourbitadder_3_carryout[3]));
  // Probe on A
  and and_16 (Product[0], B[0], A[0]);
  // Probe on Product

  // Notes on the sheet:
  //   8 Bit Multiplier 
endmodule

module EightBitMulti (
  input  [7:0] A,
  input  [7:0] B,
  output [15:0] Product,
  output C_out
);

  wire [3:0] undriven_2, undriven_3, undriven_4, undriven_5;
  wire [7:0] fourbitmulti_1_product, fourbitmulti_2_product, fourbitmulti_3_product, fourbitmulti_4_product,
       undriven, undriven_6;
  wire [15:0] sixteenbitadder_1_sum, sixteenbitadder_2_sum;

  // Probe on A
  // Probe on B
  fourBitMulti fourbitmulti_1 (.B(B[3:0]), .A(A[7:4]), .Product(fourbitmulti_1_product));
  fourBitMulti fourbitmulti_2 (.B(B[7:4]), .A(A[7:4]), .Product(fourbitmulti_2_product));
  // Probe on fourbitmulti_3_product
  fourBitMulti fourbitmulti_3 (.B(B[3:0]), .A(A[3:0]), .Product(fourbitmulti_3_product));
  fourBitMulti fourbitmulti_4 (.B(B[7:4]), .A(A[3:0]), .Product(fourbitmulti_4_product));
  // Probe on fourbitmulti_4_product
  // Probe on fourbitmulti_1_product
  // Probe on fourbitmulti_2_product
  SixteenBitAdder sixteenbitadder_1 (
    .A({undriven, fourbitmulti_3_product}), .B({undriven_5, fourbitmulti_4_product, undriven_4}),
    .Sum(sixteenbitadder_1_sum));  // open: CarryIn, CarryOut
  SixteenBitAdder sixteenbitadder_2 (
    .A({undriven_3, fourbitmulti_1_product, undriven_2}), .B({fourbitmulti_2_product, undriven_6}),
    .Sum(sixteenbitadder_2_sum));  // open: CarryIn, CarryOut
  // Probe on Product
  SixteenBitAdder sixteenbitadder_3 (
    .A(sixteenbitadder_1_sum), .B(sixteenbitadder_2_sum), .Sum(Product), .CarryOut(C_out));  // open: CarryIn
endmodule

module eightBitRegister (
  input  clock,
  input  WE,
  input  [7:0] in_3,
  input  [7:0] Din,
  input  OE,
  output [7:0] out_6
);

  Memory_Cell memory_cell_1 (
    .clock(clock), .WE(WE), .Din(Din[0]), .OE(OE), .Dout(in_3[0]), .Stored_Data(out_6[0]));  // open: Reset
  Memory_Cell memory_cell_2 (
    .clock(clock), .WE(WE), .Din(Din[1]), .OE(OE), .Dout(in_3[1]), .Stored_Data(out_6[1]));  // open: Reset
  Memory_Cell memory_cell_3 (
    .clock(clock), .WE(WE), .Din(Din[2]), .OE(OE), .Dout(in_3[2]), .Stored_Data(out_6[2]));  // open: Reset
  Memory_Cell memory_cell_4 (
    .clock(clock), .WE(WE), .Din(Din[3]), .OE(OE), .Dout(in_3[3]), .Stored_Data(out_6[3]));  // open: Reset
  Memory_Cell memory_cell_5 (
    .clock(clock), .WE(WE), .Din(Din[4]), .OE(OE), .Dout(in_3[4]), .Stored_Data(out_6[4]));  // open: Reset
  Memory_Cell memory_cell_6 (
    .clock(clock), .WE(WE), .Din(Din[5]), .OE(OE), .Dout(in_3[5]), .Stored_Data(out_6[5]));  // open: Reset
  Memory_Cell memory_cell_7 (
    .clock(clock), .WE(WE), .Din(Din[6]), .OE(OE), .Dout(in_3[6]), .Stored_Data(out_6[6]));  // open: Reset
  Memory_Cell memory_cell_8 (
    .clock(clock), .WE(WE), .Din(Din[7]), .OE(OE), .Dout(in_3[7]), .Stored_Data(out_6[7]));  // open: Reset

  // Notes on the sheet:
  //   0
  //   1
  //   2
  //   3
  //   4
  //   5
  //   6
  //   7
  //   Dout
  //   Stored data
endmodule

module MAR (
  input  clock,
  input  [3:0] Dout,
  input  WE,
  input  [3:0] in_4,
  input  in_5,
  output [3:0] out_6
);

  Memory_Cell memory_cell_1 (
    .clock(clock), .WE(WE), .Din(in_4[0]), .OE(in_5), .Dout(Dout[0]), .Stored_Data(out_6[0]));  // open: Reset
  Memory_Cell memory_cell_2 (
    .clock(clock), .WE(WE), .Din(in_4[1]), .OE(in_5), .Dout(Dout[1]), .Stored_Data(out_6[1]));  // open: Reset
  Memory_Cell memory_cell_3 (
    .clock(clock), .WE(WE), .Din(in_4[2]), .OE(in_5), .Dout(Dout[2]), .Stored_Data(out_6[2]));  // open: Reset
  Memory_Cell memory_cell_4 (
    .clock(clock), .WE(WE), .Din(in_4[3]), .OE(in_5), .Dout(Dout[3]), .Stored_Data(out_6[3]));  // open: Reset

  // Notes on the sheet:
  //   stored data
endmodule

module ALU (
  input  Flag,
  input  [4:0] Op_C0de,
  input  [15:0] A,
  input  [15:0] B,
  output [15:0] Overflow,
  output [15:0] Result
);

  wire com_8_1_a_equal_b, controlled_buffer_3_out, controlled_buffer_4_out, decodr_1_p22, not_1_out,
       sixteenbitadd_sub_1_carryout;
  wire [7:0] bit_extender_1_out;
  wire [15:0] and_operation_1_and_result, bit_extender_2_out, controlled_buffer_1_out, decodr_1_p8,
       decodr_1_p9, decodr_1_p10, decodr_1_p11, decodr_1_p12, decodr_1_p13, decodr_1_p14, decodr_1_p15,
       decodr_1_p16, decodr_1_p17, decodr_1_p18, decodr_1_p19, decodr_1_p20, decodr_1_p21,
       eightbitmulti_1_product, not_operation_1_out_2, sixteenbitadd_sub_1_result,
       sixteenbitcomparator_1_result, xor_opeation_1_xor_result;

  // Probe on A
  // Probe on B
  assign bit_extender_1_out = {{3{Op_C0de[4]}}, Op_C0de};  // Bit_Extender bit_extender_1
  assign bit_extender_2_out = {{15{Flag}}, Flag};  // Bit_Extender bit_extender_2
  com_8 com_8_1 (.A(8'h1), .B(bit_extender_1_out), .A_EQUAL_B(com_8_1_a_equal_b));  // open: A_GREATER_B, A_LESS_B
  SixteenBitAdd_Sub sixteenbitadd_sub_1 (
    .CarryIn(Flag), .A(A), .B(B), .Sub(bit_extender_2_out), .Result(sixteenbitadd_sub_1_result),
    .CarryOut(sixteenbitadd_sub_1_carryout));
  EightBitMulti eightbitmulti_1 (.A(A[7:0]), .B(B[7:0]), .Product(eightbitmulti_1_product));  // open: C_out
  SixteenBitComparator sixteenbitcomparator_1 (.A(A), .B(B), .result(sixteenbitcomparator_1_result));
  AND_operation and_operation_1 (.A(A), .B(B), .AND_result(and_operation_1_and_result));
  XOR_opeation xor_opeation_1 (.A(A), .B(B), .XOR_result(xor_opeation_1_xor_result));
  NOT_operation not_operation_1 (.A(A), .out_2(not_operation_1_out_2));
  assign controlled_buffer_1_out = Flag ? sixteenbitadd_sub_1_result : 16'bz;  // Controlled_Buffer controlled_buffer_1
  not not_1 (not_1_out, Flag);
  assign controlled_buffer_1_out = not_1_out ? sixteenbitadd_sub_1_result : 16'bz;  // Controlled_Buffer controlled_buffer_2
  // Decodr decodr_1: pin names not known; wires that end beside it: controlled_buffer_1_out, eightbitmulti_1_product, sixteenbitcomparator_1_result, and_operation_1_and_result, xor_opeation_1_xor_result, not_operation_1_out_2, Op_C0de, decodr_1_p8, decodr_1_p9, decodr_1_p10, decodr_1_p11, decodr_1_p12, decodr_1_p13, decodr_1_p14, decodr_1_p15, decodr_1_p16, decodr_1_p17, decodr_1_p18, decodr_1_p19, decodr_1_p20, decodr_1_p21, decodr_1_p22
  assign controlled_buffer_3_out = com_8_1_a_equal_b ? sixteenbitadd_sub_1_carryout : 1'bz;  // Controlled_Buffer controlled_buffer_3
  assign controlled_buffer_4_out = not_1_out ? controlled_buffer_3_out : 1'bz;  // Controlled_Buffer controlled_buffer_4
  assign Overflow = {{15{1'b0}}, controlled_buffer_4_out};  // Bit_Extender bit_extender_3
  // Probe on Overflow
  assign Result = decodr_1_p8 | decodr_1_p9 | decodr_1_p10 | decodr_1_p11 | decodr_1_p12 | decodr_1_p13 | decodr_1_p14 | decodr_1_p15 | decodr_1_p16 | decodr_1_p17 | decodr_1_p18 | decodr_1_p19 | decodr_1_p20 | decodr_1_p21;  // OR_Gate or_1, 16 bits wide
  // Probe on Result
endmodule

module EightBitCPU (
  input  counter_OE,
  input  OE,
  input  [7:0] testing_data,
  input  [3:0] OE_Testing_data,
  input  OE_testing_data_2,
  input  count_enable,
  input  WE,
  input  WE_2,
  input  OE_2,
  input  Internal_OE,
  input  OE_3,
  input  WE_3,
  input  OE_4,
  input  WE_4,
  input  OE_5,
  input  WE_5,
  input  WE_6,
  input  OE_6,
  input  OE_7,
  input  WE_7,
  output [3:0] content_of_count,
  output [3:0] MAR_Content,
  output [7:0] IR,
  output [7:0] MBR_Content,
  output [7:0] Reg_A_content,
  output [7:0] ALU_result,
  output [7:0] out_27,
  output [7:0] Reg_B_content
);

  wire clock_1_out;
  wire [3:0] controlled_buffer_1_out, controlled_buffer_4_out;
  wire [7:0] controlled_buffer_2_out, undriven;

  Counter #(.max('hf), .width(4)) counter_1 (
    .D(controlled_buffer_1_out), .count(count_enable), .Q(content_of_count), .clk(clock_1_out));  // open: load, carry, up, clr
  Clock clock_1 (.out(clock_1_out));
  assign controlled_buffer_1_out = counter_OE ? content_of_count : 4'bz;  // Controlled_Buffer controlled_buffer_1
  eightBitRegister eightbitregister_1 (
    .clock(clock_1_out), .WE(WE_3), .Din(controlled_buffer_2_out), .OE(OE_4), .in_3(undriven), .out_6(IR));
  eightBitRegister eightbitregister_2 (
    .clock(clock_1_out), .WE(WE_5), .Din(controlled_buffer_2_out), .out_6(Reg_A_content));  // open: OE, in_3
  eightBitRegister eightbitregister_3 (
    .clock(clock_1_out), .WE(WE_7), .Din(controlled_buffer_2_out));  // open: OE, in_3, out_6
  BitSelector #(.group(4)) bitselector_1 (.in(undriven), .out(controlled_buffer_1_out), .sel(1'b0));
  // Probe on Reg_A_content
  // Probe on Reg_B_content
  // Probe on ALU_result
  LED led_1 (.in(controlled_buffer_2_out[7]));
  LED led_2 (.in(controlled_buffer_2_out[6]));
  LED led_3 (.in(controlled_buffer_2_out[5]));
  LED led_4 (.in(controlled_buffer_2_out[4]));
  assign controlled_buffer_2_out = OE_testing_data_2 ? testing_data : 8'bz;  // Controlled_Buffer controlled_buffer_2
  LED led_5 (.in(controlled_buffer_2_out[3]));
  LED led_6 (.in(controlled_buffer_2_out[2]));
  LED led_7 (.in(controlled_buffer_2_out[1]));
  LED led_8 (.in(controlled_buffer_2_out[0]));
  eightBitRegister eightbitregister_4 (
    .clock(clock_1_out), .WE(WE_6), .Din(controlled_buffer_2_out), .OE(OE_7), .in_3(controlled_buffer_2_out),
    .out_6(out_27));
  MAR mar_1 (
    .clock(clock_1_out), .WE(WE), .in_4(controlled_buffer_1_out), .in_5(OE_2),
    .Dout(controlled_buffer_4_out), .out_6(MAR_Content));
  assign controlled_buffer_2_out = Internal_OE ? MBR_Content : 8'bz;  // Controlled_Buffer controlled_buffer_3
  eightBitRegister eightbitregister_5 (
    .clock(clock_1_out), .WE(WE_4), .Din(controlled_buffer_2_out), .OE(OE_5), .in_3(controlled_buffer_2_out),
    .out_6(MBR_Content));
  // Probe on out_27
  assign controlled_buffer_4_out = OE ? OE_Testing_data : 4'bz;  // Controlled_Buffer controlled_buffer_4
  LED led_9 (.in(controlled_buffer_2_out[7]));
  LED led_10 (.in(controlled_buffer_2_out[6]));
  LED led_11 (.in(controlled_buffer_2_out[5]));
  LED led_12 (.in(controlled_buffer_2_out[4]));
  LED led_13 (.in(controlled_buffer_2_out[3]));
  LED led_14 (.in(controlled_buffer_2_out[2]));
  LED led_15 (.in(controlled_buffer_2_out[1]));
  LED led_16 (.in(controlled_buffer_2_out[0]));
  RAM #(.addrWidth(4)) ram_1 (
    .addr(controlled_buffer_4_out), .we(WE_2), .oe(OE_3), .clk(clock_1_out), .din(controlled_buffer_2_out),
    .dout(controlled_buffer_2_out));

  // Notes on the sheet:
  //   PC
  //   Reg A
  //   ALU
  //   Reg B
  //   IR content 
  //   D7
  //   D6
  //   internal address bus 
  //   D5
  //   D4
  //   D3
  //   D2
  //   internal data bus
  //   D1
  //   D0
  //   MBR
  //   Output R
  //   MAR
  //   output content
  //   External  address bus
  //   D7
  //   D6
  //   D5
  //   D4
  //   External data bus
  //   D3
  //   D2
  //   D1
  //   D0
endmodule

module comprator4BiT (
  input  [3:0] A,
  input  [3:0] B,
  output AgreaterB,
  output AequalsB,
  output AlessB
);

  wire and_1_out, and_2_out, and_3_out, and_4_out, and_5_out, and_6_out, and_7_out, and_8_out, not_1_out,
       not_2_out, not_3_out, not_4_out, not_5_out, not_6_out, not_7_out, not_8_out, xnor_1_out, xnor_2_out,
       xnor_3_out, xnor_4_out;

  // Probe on A
  // Probe on B
  not not_1 (not_1_out, B[0]);
  not not_2 (not_2_out, B[1]);
  not not_3 (not_3_out, B[2]);
  not not_4 (not_4_out, A[3]);
  not not_5 (not_5_out, A[2]);
  not not_6 (not_6_out, A[0]);
  not not_7 (not_7_out, B[3]);
  xnor xnor_1 (xnor_1_out, A[0], B[0]);
  xnor xnor_2 (xnor_2_out, A[1], B[1]);
  xnor xnor_3 (xnor_3_out, A[2], B[2]);
  xnor xnor_4 (xnor_4_out, A[3], B[3]);
  not not_8 (not_8_out, A[1]);
  and and_1 (and_1_out, not_1_out, A[0], xnor_3_out, xnor_4_out);
  and and_2 (and_2_out, not_2_out, A[1], xnor_3_out, xnor_4_out);
  and and_3 (and_3_out, not_3_out, A[2], xnor_4_out);
  and and_4 (and_4_out, not_7_out, A[3]);
  and and_5 (and_5_out, B[3], not_4_out);
  and and_6 (and_6_out, xnor_4_out, B[2], not_5_out);
  and and_7 (and_7_out, xnor_4_out, xnor_3_out, B[1], not_8_out);
  and and_8 (and_8_out, xnor_4_out, xnor_3_out, not_6_out, B[0]);
  and and_9 (AequalsB, xnor_1_out, xnor_2_out, xnor_3_out, xnor_4_out);
  or or_1 (AgreaterB, and_1_out, and_2_out, and_3_out, and_4_out);
  or or_2 (AlessB, and_5_out, and_6_out, and_7_out, and_8_out);

  // Notes on the sheet:
  //   A<B
  //   A>B
  //   A=B
endmodule

module comprator8Bit (
  input  [7:0] A,
  input  [7:0] B,
  output AequalB,
  output AgreaterB,
  output BgreaterA
);

  wire and_1_out, and_2_out, comprator4bit_1_aequalsb, comprator4bit_1_agreaterb, comprator4bit_1_alessb,
       comprator4bit_2_aequalsb, comprator4bit_2_agreaterb, comprator4bit_2_alessb;

  // Probe on A
  // Probe on B
  comprator4BiT comprator4bit_1 (
    .A(A[3:0]), .B(B[3:0]), .AgreaterB(comprator4bit_1_agreaterb), .AequalsB(comprator4bit_1_aequalsb),
    .AlessB(comprator4bit_1_alessb));
  comprator4BiT comprator4bit_2 (
    .A(A[7:4]), .B(B[7:4]), .AgreaterB(comprator4bit_2_agreaterb), .AequalsB(comprator4bit_2_aequalsb),
    .AlessB(comprator4bit_2_alessb));
  and and_1 (and_1_out, comprator4bit_1_alessb, comprator4bit_2_aequalsb);
  and and_2 (and_2_out, comprator4bit_1_agreaterb, comprator4bit_2_aequalsb);
  and and_3 (AequalB, comprator4bit_1_aequalsb, comprator4bit_2_aequalsb);
  or or_1 (AgreaterB, comprator4bit_2_agreaterb, and_2_out);
  or or_2 (BgreaterA, and_1_out, comprator4bit_2_alessb);

  // Notes on the sheet:
  //   LSB
  //   MSB
  //   A=B
  //   A>B
  //   B>A
endmodule

module SixteenBitComparator (
  input  [15:0] A,
  input  [15:0] B,
  output [15:0] result
);

  wire and_1_out, and_2_out, and_3_out, comprator8bit_1_aequalb, comprator8bit_1_agreaterb,
       comprator8bit_1_bgreatera, comprator8bit_2_aequalb, comprator8bit_2_agreaterb,
       comprator8bit_2_bgreatera, or_1_out, or_2_out;
  wire [2:0] controlled_buffer_1_out;

  // Probe on A
  // Probe on B
  comprator8Bit comprator8bit_1 (
    .A(A[7:0]), .B(B[7:0]), .AequalB(comprator8bit_1_aequalb), .AgreaterB(comprator8bit_1_agreaterb),
    .BgreaterA(comprator8bit_1_bgreatera));
  comprator8Bit comprator8bit_2 (
    .A(A[15:8]), .B(B[15:8]), .AequalB(comprator8bit_2_aequalb), .AgreaterB(comprator8bit_2_agreaterb),
    .BgreaterA(comprator8bit_2_bgreatera));
  and and_1 (and_1_out, comprator8bit_1_agreaterb, comprator8bit_2_aequalb);
  and and_2 (and_2_out, comprator8bit_2_aequalb, comprator8bit_1_bgreatera);
  or or_1 (or_1_out, and_1_out, comprator8bit_2_agreaterb);
  and and_3 (and_3_out, comprator8bit_2_aequalb, comprator8bit_1_aequalb);
  or or_2 (or_2_out, comprator8bit_2_bgreatera, and_2_out);
  assign controlled_buffer_1_out = or_1_out ? 3'b100 : 3'bz;  // Controlled_Buffer controlled_buffer_1
  assign controlled_buffer_1_out = and_3_out ? 3'b010 : 3'bz;  // Controlled_Buffer controlled_buffer_2
  assign controlled_buffer_1_out = or_2_out ? 3'b001 : 3'bz;  // Controlled_Buffer controlled_buffer_3
  // Probe on result
  assign result = {{13{1'b0}}, controlled_buffer_1_out};  // Bit_Extender bit_extender_1

  // Notes on the sheet:
  //   LSB
  //   MSB
endmodule

module Decodr (
  input  [15:0] Reserved,
  input  [15:0] Sum_OR_Sub,
  input  [15:0] mult,
  input  [15:0] Store_oR_store_overflow,
  input  [15:0] From_A_to_B,
  input  [15:0] Swap_source_with_destination,
  input  [15:0] Block_load,
  input  [15:0] Block_store,
  input  [15:0] Mat_Mult,
  input  [15:0] Comparator,
  input  [15:0] AND_operation,
  input  [15:0] XOR_operation,
  input  [15:0] NOT_A,
  input  [15:0] NOP_or_HAlT,
  input  [4:0] Op_code,
  output [15:0] out_16,
  output [15:0] out_17,
  output [15:0] out_18,
  output [15:0] out_19,
  output [15:0] out_20,
  output [15:0] out_21,
  output [15:0] out_22,
  output [15:0] out_23,
  output [15:0] out_24,
  output [15:0] out_25,
  output [15:0] out_26,
  output [15:0] out_27,
  output [15:0] out_28,
  output [15:0] out_29
);

  wire and_1_out, and_2_out, and_3_out, and_4_out, and_5_out, and_6_out, and_7_out, and_8_out, and_9_out,
       and_10_out, and_11_out, and_12_out, and_13_out, and_14_out, not_1_out, not_2_out, not_3_out, not_4_out;
  wire [15:0] bit_extender_1_out, bit_extender_2_out, bit_extender_3_out, bit_extender_4_out,
       bit_extender_5_out, bit_extender_6_out, bit_extender_7_out, bit_extender_8_out, bit_extender_9_out,
       bit_extender_10_out, bit_extender_11_out, bit_extender_12_out, bit_extender_13_out,
       bit_extender_14_out;

  not not_1 (not_1_out, Op_code[0]);
  not not_2 (not_2_out, Op_code[1]);
  not not_3 (not_3_out, Op_code[2]);
  not not_4 (not_4_out, Op_code[3]);
  and and_1 (and_1_out, not_1_out, not_2_out, not_3_out, not_4_out);
  and and_2 (and_2_out, not_2_out, not_3_out, not_4_out, Op_code[0]);
  and and_3 (and_3_out, not_3_out, not_3_out, Op_code[0], Op_code[1]);
  and and_4 (and_4_out, not_1_out, not_2_out, Op_code[2], not_4_out);
  and and_5 (and_5_out, not_2_out, not_4_out, Op_code[0], Op_code[2]);
  and and_6 (and_6_out, not_1_out, not_4_out, Op_code[1], Op_code[2]);
  and and_7 (and_7_out, not_4_out, Op_code[0], Op_code[1], Op_code[2]);
  and and_8 (and_8_out, not_1_out, not_2_out, not_3_out, Op_code[3]);
  and and_9 (and_9_out, not_2_out, not_3_out, Op_code[0], Op_code[3]);
  and and_10 (and_10_out, not_1_out, not_3_out, Op_code[1], Op_code[3]);
  and and_11 (and_11_out, not_3_out, Op_code[0], Op_code[1], Op_code[3]);
  and and_12 (and_12_out, not_1_out, not_2_out, Op_code[2], Op_code[3]);
  and and_13 (and_13_out, not_2_out, Op_code[0], Op_code[2], Op_code[3]);
  and and_14 (and_14_out, not_1_out, Op_code[1], Op_code[2], Op_code[3]);
  assign bit_extender_1_out = {{15{and_1_out}}, and_1_out};  // Bit_Extender bit_extender_1
  assign bit_extender_2_out = {{15{and_2_out}}, and_2_out};  // Bit_Extender bit_extender_2
  assign bit_extender_3_out = {{15{and_3_out}}, and_3_out};  // Bit_Extender bit_extender_3
  assign bit_extender_4_out = {{15{and_4_out}}, and_4_out};  // Bit_Extender bit_extender_4
  assign bit_extender_5_out = {{15{and_5_out}}, and_5_out};  // Bit_Extender bit_extender_5
  assign bit_extender_6_out = {{15{and_6_out}}, and_6_out};  // Bit_Extender bit_extender_6
  assign bit_extender_7_out = {{15{and_7_out}}, and_7_out};  // Bit_Extender bit_extender_7
  assign bit_extender_8_out = {{15{and_8_out}}, and_8_out};  // Bit_Extender bit_extender_8
  assign bit_extender_9_out = {{15{and_9_out}}, and_9_out};  // Bit_Extender bit_extender_9
  assign bit_extender_10_out = {{15{and_10_out}}, and_10_out};  // Bit_Extender bit_extender_10
  assign bit_extender_11_out = {{15{and_11_out}}, and_11_out};  // Bit_Extender bit_extender_11
  assign bit_extender_12_out = {{15{and_12_out}}, and_12_out};  // Bit_Extender bit_extender_12
  assign bit_extender_13_out = {{15{and_13_out}}, and_13_out};  // Bit_Extender bit_extender_13
  assign bit_extender_14_out = {{15{and_14_out}}, and_14_out};  // Bit_Extender bit_extender_14
  assign out_16 = bit_extender_1_out & Reserved;  // AND_Gate and_15, 16 bits wide
  assign out_17 = bit_extender_2_out & Sum_OR_Sub;  // AND_Gate and_16, 16 bits wide
  assign out_18 = bit_extender_3_out & mult;  // AND_Gate and_17, 16 bits wide
  assign out_19 = bit_extender_4_out & Store_oR_store_overflow;  // AND_Gate and_18, 16 bits wide
  assign out_20 = bit_extender_5_out & From_A_to_B;  // AND_Gate and_19, 16 bits wide
  assign out_21 = bit_extender_6_out & Swap_source_with_destination;  // AND_Gate and_20, 16 bits wide
  assign out_22 = bit_extender_7_out & Block_load;  // AND_Gate and_21, 16 bits wide
  assign out_23 = bit_extender_8_out & Block_store;  // AND_Gate and_22, 16 bits wide
  assign out_24 = bit_extender_9_out & Mat_Mult;  // AND_Gate and_23, 16 bits wide
  assign out_25 = bit_extender_10_out & Comparator;  // AND_Gate and_24, 16 bits wide
  assign out_26 = bit_extender_11_out & AND_operation;  // AND_Gate and_25, 16 bits wide
  assign out_27 = bit_extender_12_out & XOR_operation;  // AND_Gate and_26, 16 bits wide
  assign out_28 = bit_extender_13_out & NOT_A;  // AND_Gate and_27, 16 bits wide
  assign out_29 = bit_extender_14_out & NOP_or_HAlT;  // AND_Gate and_28, 16 bits wide

  // Notes on the sheet:
  //   0000
  //   0001
  //   0011
  //   0100
  //   0101
  //   0110
  //   0111
  //   1000
  //   1001
  //   1010
  //   1011
  //   1100
  //   1101
  //   1110
  //   0000
  //   0001
  //   0011
  //   0100
  //   0101
  //   0110
  //   0111
  //   `1000
  //   1001
  //   1010
  //   1011
  //   1100
  //   1101
  //   1110
endmodule

module CPU_16_Circuit (
);

  wire and_1_out, Clock_runner_out, com16bitnormal_1_equal, controlled_buffer_12_out,
       Instruction_Splliter_flag, Instruction_Splliter_nop, not_1_out, not_2_out, or_1_out, or_2_out,
       ram_controler_1_a, ram_controler_1_b;
  wire [3:0] Step_counter_q;
  wire [4:0] bus_terminal_like_circuit_1_add_a, bus_terminal_like_circuit_1_add_b, controlled_buffer_15_out,
       controlled_buffer_24_out, controlled_buffer_26_out, counter_1_q, counter_2_q, counter_3_q,
       counter_4_q, counter_5_q, Instruction_Splliter_add_a, Instruction_Splliter_add_b,
       Instruction_Splliter_opcode, MAR_A_q, MAR_B_q, MAR_Z_q, Program_counter_q, register_1_q;
  wire [15:0] alu_1_overflow, alu_1_result, bus_terminal_like_circuit_1_a_value,
       bus_terminal_like_circuit_1_b_value, controlled_buffer_1_out, controlled_buffer_5_out,
       controlled_buffer_9_out, controlled_buffer_14_out, controlled_buffer_21_out, controlled_buffer_22_out,
       mat_mult_1_r0, mat_mult_1_r1, mat_mult_1_r2, mat_mult_1_r3, MBR_A_q, MBR_B_q, MBR_Z_q, Overflow_Reg_q,
       R0_q, R1_q, R2_q, R3_q, ram_1_dout, ram_2_dout, ram_3_dout, ram_4_dout, Reg_A1_q, Reg_A2_q, Reg_A3_q,
       Reg_A_0_q, REG_B0_q, REG_B1_q, REG_B2_q, REG_B3_q, Reg_Output_q, register_2_q, register_3_q,
       register_swap_1_reg_a0, register_swap_1_reg_a1, register_swap_1_reg_a2, register_swap_1_reg_a3,
       register_swap_1_reg_b0, register_swap_1_reg_b1, register_swap_1_reg_b2, register_swap_1_reg_b3;
  wire [31:0] rom_1_data, rom_2_data;

  // Probe on controlled_buffer_1_out
  // Probe on mat_mult_1_r0
  // Probe on mat_mult_1_r2
  // Probe on mat_mult_1_r1
  // Probe on mat_mult_1_r3
  assign controlled_buffer_1_out = rom_2_data[23] ? R3_q : 16'bz;  // Controlled_Buffer controlled_buffer_1
  assign controlled_buffer_1_out = rom_2_data[24] ? R2_q : 16'bz;  // Controlled_Buffer controlled_buffer_2
  assign controlled_buffer_1_out = rom_2_data[25] ? R1_q : 16'bz;  // Controlled_Buffer controlled_buffer_3
  assign controlled_buffer_1_out = rom_2_data[26] ? R0_q : 16'bz;  // Controlled_Buffer controlled_buffer_4
  MAt_mult mat_mult_1 (
    .A0(Reg_A_0_q), .A1(Reg_A1_q), .A2(Reg_A2_q), .A3(Reg_A3_q), .B0(REG_B0_q), .B1(REG_B1_q), .B2(REG_B2_q),
    .B3(REG_B3_q), .R0(mat_mult_1_r0), .R1(mat_mult_1_r1), .R2(mat_mult_1_r2), .R3(mat_mult_1_r3));
  Register_swap register_swap_1 (
    .OPCODE(Instruction_Splliter_opcode), .RegA0(Reg_A_0_q), .RegA1(Reg_A1_q), .RegA2(Reg_A2_q),
    .RegA3(Reg_A3_q), .RegB0(REG_B0_q), .RegB1(REG_B1_q), .RegB2(REG_B2_q), .RegB3(REG_B3_q),
    .Address_A(Instruction_Splliter_add_a), .Address_B(Instruction_Splliter_add_b),
    .REG_B0(register_swap_1_reg_b0), .REG_B1(register_swap_1_reg_b1), .REG_B2(register_swap_1_reg_b2),
    .REG_B3(register_swap_1_reg_b3), .REG_A0(register_swap_1_reg_a0), .REG_A1(register_swap_1_reg_a1),
    .REG_A2(register_swap_1_reg_a2), .REG_A3(register_swap_1_reg_a3));
  assign controlled_buffer_5_out = rom_2_data[12] ? register_swap_1_reg_a3 : 16'bz;  // Controlled_Buffer controlled_buffer_5
  Register #(.width(16)) R1 (
    .D(mat_mult_1_r1), .en(rom_2_data[27]), .clk(controlled_buffer_12_out), .Q(R1_q));  // open: clr
  Register #(.width(16)) R3 (
    .D(mat_mult_1_r3), .en(rom_2_data[27]), .clk(controlled_buffer_12_out), .Q(R3_q));  // open: clr
  assign controlled_buffer_5_out = rom_2_data[15] ? register_swap_1_reg_a0 : 16'bz;  // Controlled_Buffer controlled_buffer_6
  assign controlled_buffer_5_out = rom_2_data[14] ? register_swap_1_reg_a1 : 16'bz;  // Controlled_Buffer controlled_buffer_7
  assign controlled_buffer_5_out = rom_2_data[13] ? register_swap_1_reg_a2 : 16'bz;  // Controlled_Buffer controlled_buffer_8
  assign controlled_buffer_9_out = rom_2_data[10] ? register_swap_1_reg_b1 : 16'bz;  // Controlled_Buffer controlled_buffer_9
  assign controlled_buffer_9_out = rom_2_data[9] ? register_swap_1_reg_b2 : 16'bz;  // Controlled_Buffer controlled_buffer_10
  assign controlled_buffer_9_out = rom_2_data[8] ? register_swap_1_reg_b3 : 16'bz;  // Controlled_Buffer controlled_buffer_11
  Register #(.width(16)) R0 (
    .D(mat_mult_1_r0), .en(rom_2_data[27]), .clk(controlled_buffer_12_out), .Q(R0_q));  // open: clr
  Clock Clock_runner (.out(Clock_runner_out));
  assign controlled_buffer_12_out = not_1_out ? Clock_runner_out : 1'bz;  // Controlled_Buffer controlled_buffer_12
  not not_1 (not_1_out, Instruction_Splliter_nop);
  assign controlled_buffer_9_out = rom_2_data[11] ? register_swap_1_reg_b0 : 16'bz;  // Controlled_Buffer controlled_buffer_13
  Register #(.width(16)) R2 (
    .D(mat_mult_1_r2), .en(rom_2_data[27]), .clk(controlled_buffer_12_out), .Q(R2_q));  // open: clr
  COm16bitNORmal com16bitnormal_1 (
    .A(alu_1_overflow), .B(16'h1), .Equal(com16bitnormal_1_equal));  // open: A_G_B, B_G_A
  and and_1 (and_1_out, rom_1_data[14], com16bitnormal_1_equal);
  Counter #(.max('hf), .width(5)) Program_counter (
    .up(1'b1), .count(rom_1_data[31]), .clk(controlled_buffer_12_out), .Q(Program_counter_q));  // open: clr, load, D, carry
  ALU alu_1 (
    .Flag(Instruction_Splliter_flag), .Op_C0de(register_1_q), .A(Reg_A_0_q), .B(REG_B0_q),
    .Overflow(alu_1_overflow), .Result(alu_1_result));
  Register #(.width(16)) Overflow_Reg (
    .D(alu_1_overflow), .en(and_1_out), .clk(controlled_buffer_12_out), .Q(Overflow_Reg_q));  // open: clr
  assign controlled_buffer_14_out = Instruction_Splliter_flag ? Overflow_Reg_q : 16'bz;  // Controlled_Buffer controlled_buffer_14
  Register #(.width(16)) Reg_A_0 (
    .D(controlled_buffer_5_out), .en(rom_1_data[16]), .clk(controlled_buffer_12_out), .Q(Reg_A_0_q));  // open: clr
  Register #(.width(16)) Reg_A2 (
    .D(controlled_buffer_5_out), .en(rom_1_data[8]), .clk(controlled_buffer_12_out), .Q(Reg_A2_q));  // open: clr
  Register #(.width(16)) REG_B1 (
    .D(controlled_buffer_9_out), .en(rom_1_data[6]), .clk(controlled_buffer_12_out), .Q(REG_B1_q));  // open: clr
  Register #(.width(16)) REG_B3 (
    .D(controlled_buffer_9_out), .en(rom_1_data[4]), .clk(controlled_buffer_12_out), .Q(REG_B3_q));  // open: clr
  InstSPILLTER Instruction_Splliter (
    .Instruction(controlled_buffer_22_out), .Write_Enable(rom_1_data[26]), .clock(controlled_buffer_12_out),
    .Add_B(Instruction_Splliter_add_b), .Add_A(Instruction_Splliter_add_a),
    .Opcode(Instruction_Splliter_opcode), .Flag(Instruction_Splliter_flag), .NOP(Instruction_Splliter_nop));
  not not_2 (not_2_out, Instruction_Splliter_flag);
  Register #(.width(16)) REG_B0 (
    .D(controlled_buffer_9_out), .en(rom_1_data[15]), .clk(controlled_buffer_12_out), .Q(REG_B0_q));  // open: clr
  assign controlled_buffer_15_out = rom_2_data[22] ? Program_counter_q : 5'bz;  // Controlled_Buffer controlled_buffer_15
  Register #(.width(5)) register_1 (
    .D(Instruction_Splliter_opcode), .en(rom_1_data[25]), .clk(controlled_buffer_12_out), .Q(register_1_q));  // open: clr
  Register #(.width(16)) Reg_A1 (
    .D(controlled_buffer_5_out), .en(rom_1_data[9]), .clk(controlled_buffer_12_out), .Q(Reg_A1_q));  // open: clr
  Register #(.width(16)) REG_B2 (
    .D(controlled_buffer_9_out), .en(rom_1_data[5]), .clk(controlled_buffer_12_out), .Q(REG_B2_q));  // open: clr
  assign controlled_buffer_15_out = rom_2_data[21] ? Instruction_Splliter_add_a : 5'bz;  // Controlled_Buffer controlled_buffer_16
  assign controlled_buffer_15_out = rom_2_data[6] ? Instruction_Splliter_add_b : 5'bz;  // Controlled_Buffer controlled_buffer_17
  Register #(.width(16)) Reg_A3 (
    .D(controlled_buffer_5_out), .en(rom_1_data[7]), .clk(controlled_buffer_12_out), .Q(Reg_A3_q));  // open: clr
  Register #(.width(5)) MAR_Z (
    .D(controlled_buffer_15_out), .en(rom_1_data[30]), .clk(controlled_buffer_12_out), .Q(MAR_Z_q));  // open: clr
  Register #(.width(16)) Reg_Output (
    .D(alu_1_result), .en(rom_1_data[14]), .clk(controlled_buffer_12_out), .Q(Reg_Output_q));  // open: clr
  Register #(.width(5)) MAR_A (
    .D(Instruction_Splliter_add_a), .en(rom_1_data[24]), .clk(controlled_buffer_12_out), .Q(MAR_A_q));  // open: clr
  assign controlled_buffer_1_out = rom_1_data[29] ? ram_2_dout : 16'bz;  // Controlled_Buffer controlled_buffer_18
  assign controlled_buffer_1_out = rom_1_data[10] ? controlled_buffer_14_out : 16'bz;  // Controlled_Buffer controlled_buffer_19
  assign controlled_buffer_14_out = not_2_out ? Reg_Output_q : 16'bz;  // Controlled_Buffer controlled_buffer_20
  Register #(.width(16)) MBR_Z (
    .D(controlled_buffer_21_out), .en(rom_1_data[28]), .clk(controlled_buffer_12_out), .Q(MBR_Z_q));  // open: clr
  assign controlled_buffer_21_out = rom_2_data[16] ? controlled_buffer_1_out : 16'bz;  // Controlled_Buffer controlled_buffer_21
  Register #(.width(5)) MAR_B (
    .D(Instruction_Splliter_add_b), .en(rom_1_data[23]), .clk(controlled_buffer_12_out), .Q(MAR_B_q));  // open: clr
  assign controlled_buffer_22_out = rom_1_data[27] ? MBR_Z_q : 16'bz;  // Controlled_Buffer controlled_buffer_22
  RAM_controler ram_controler_1 (
    .opcode(register_1_q), .Flag(Instruction_Splliter_flag), .C(rom_2_data[1]), .A(ram_controler_1_a),
    .B(ram_controler_1_b));
  Register #(.width(16)) MBR_A (
    .D(ram_1_dout), .en(rom_1_data[20]), .clk(controlled_buffer_12_out), .Q(MBR_A_q));  // open: clr
  Bus_terminal_like_circuit bus_terminal_like_circuit_1 (
    .Opcodee(register_1_q), .Data(MBR_Z_q), .Address(MAR_A_q), .Flag(Instruction_Splliter_flag),
    .Add_A(bus_terminal_like_circuit_1_add_a), .A_Value(bus_terminal_like_circuit_1_a_value),
    .Add_B(bus_terminal_like_circuit_1_add_b), .B_Value(bus_terminal_like_circuit_1_b_value));
  assign controlled_buffer_5_out = rom_1_data[18] ? MBR_A_q : 16'bz;  // Controlled_Buffer controlled_buffer_23
  Counter #(.max('h1f), .width(5)) counter_1 (
    .load(rom_2_data[3]), .D(bus_terminal_like_circuit_1_add_a), .count(rom_2_data[2]), .Q(counter_1_q),
    .up(1'b1), .clk(controlled_buffer_12_out));  // open: carry, clr
  assign controlled_buffer_24_out = ram_controler_1_a ? counter_1_q : 5'bz;  // Controlled_Buffer controlled_buffer_24
  Register #(.width(16)) MBR_B (
    .D(ram_4_dout), .en(rom_1_data[19]), .clk(controlled_buffer_12_out), .Q(MBR_B_q));  // open: clr
  Counter #(.max('h1f), .width(5)) counter_2 (
    .load(rom_2_data[3]), .D(bus_terminal_like_circuit_1_add_b), .count(rom_2_data[2]), .Q(counter_2_q),
    .up(1'b1), .clk(controlled_buffer_12_out));  // open: carry, clr
  assign controlled_buffer_9_out = rom_1_data[17] ? MBR_B_q : 16'bz;  // Controlled_Buffer controlled_buffer_25
  assign controlled_buffer_26_out = ram_controler_1_b ? counter_2_q : 5'bz;  // Controlled_Buffer controlled_buffer_26
  Counter #(.max('h1f), .width(5)) counter_3 (
    .load(rom_2_data[30]), .D(MAR_B_q), .count(rom_2_data[28]), .Q(counter_3_q), .up(1'b1),
    .clk(controlled_buffer_12_out));  // open: carry, clr
  Counter #(.max('h1f), .width(5)) counter_4 (
    .load(rom_2_data[31]), .D(MAR_A_q), .count(rom_2_data[29]), .Q(counter_4_q), .up(1'b1),
    .clk(controlled_buffer_12_out));  // open: carry, clr
  Register #(.width(16)) register_2 (
    .D(controlled_buffer_5_out), .en(rom_1_data[18]), .clk(controlled_buffer_12_out), .Q(register_2_q));  // open: clr
  Register #(.width(16)) register_3 (
    .D(controlled_buffer_9_out), .en(rom_1_data[17]), .clk(controlled_buffer_12_out), .Q(register_3_q));  // open: clr
  assign controlled_buffer_26_out = rom_2_data[4] ? counter_3_q : 5'bz;  // Controlled_Buffer controlled_buffer_27
  assign bus_terminal_like_circuit_1_b_value = rom_2_data[7] ? register_2_q : 16'bz;  // Controlled_Buffer controlled_buffer_28
  or or_1 (or_1_out, rom_2_data[7], rom_1_data[22], ram_controler_1_a);
  assign bus_terminal_like_circuit_1_a_value = rom_2_data[7] ? register_3_q : 16'bz;  // Controlled_Buffer controlled_buffer_29
  assign controlled_buffer_24_out = rom_2_data[17] ? counter_4_q : 5'bz;  // Controlled_Buffer controlled_buffer_30
  RAM #(.addrWidth(5), .dataWidth(16), .\type ("nonvolatile")) ram_1 (
    .addr(controlled_buffer_24_out), .we(or_1_out), .oe(rom_1_data[12]), .clk(controlled_buffer_12_out),
    .din(bus_terminal_like_circuit_1_a_value), .dout(ram_1_dout));
  RAM #(.addrWidth(5), .dataWidth(16), .\type ("nonvolatile")) ram_2 (
    .addr(MAR_Z_q), .we(rom_1_data[11]), .oe(rom_1_data[13]), .clk(controlled_buffer_12_out),
    .din(controlled_buffer_22_out), .dout(ram_2_dout));
  or or_2 (or_2_out, rom_2_data[7], rom_1_data[21], ram_controler_1_b);
  Counter #(.max('h1f), .width(5)) counter_5 (
    .load(rom_2_data[20]), .D(MAR_Z_q), .count(rom_2_data[19]), .Q(counter_5_q), .up(1'b1),
    .clk(controlled_buffer_12_out));  // open: carry, clr
  RAM #(.addrWidth(5), .dataWidth(16)) ram_3 (
    .addr(counter_5_q), .we(rom_1_data[3]), .oe(rom_1_data[2]), .clk(controlled_buffer_12_out),
    .din(controlled_buffer_22_out), .dout(ram_3_dout));
  RAM #(.addrWidth(5), .dataWidth(16), .\type ("nonvolatile")) ram_4 (
    .addr(controlled_buffer_26_out), .we(or_2_out), .oe(rom_1_data[1]), .clk(controlled_buffer_12_out),
    .din(bus_terminal_like_circuit_1_b_value), .dout(ram_4_dout));
  assign controlled_buffer_21_out = rom_2_data[5] ? ram_3_dout : 16'bz;  // Controlled_Buffer controlled_buffer_31
  Counter #(.max('hf), .width(4)) Step_counter (
    .clr(rom_1_data[0]), .up(1'b1), .count(1'b1), .clk(controlled_buffer_12_out), .Q(Step_counter_q));  // open: load, D, carry
  ROM #(.dataWidth(32)) rom_1 (.addr({register_1_q[3:0], Step_counter_q}), .data(rom_1_data));
  ROM #(.dataWidth(32)) rom_2 (.addr({register_1_q[3:0], Step_counter_q}), .data(rom_2_data));

  // Notes on the sheet:
  //   Mat Mult Result
  //   opcode Reg
  //   Rams WE controller
  //   C E
  //   C E
  //   counter A
  //   Counter B
  //   instruction __Ram
  //   RAM __A
  //   Counter C
  //   Program counter
  //   MAR__Z_WE
  //   INST.RAM  to MBR_CB
  //   MBR__Z_WE
  //   MBR_Z_OE
  //   spillter WE
  //   OP__code WE
  //   MAR_A_WE
  //   MAR_B_WE
  //   RAM_A_WE
  //   RAM_B_WE
  //   MBR_A_WE
  //   MBR_B_WE
  //   MBR_A_OE
  //   MBR_B_OE
  //   REG_A0_WE
  //   REG_B0_WE
  //   OUTPUT_REG_WE
  //   INSTUC_RAM_OE
  //   RAM_A_OE
  //   INSTUC_RAM_WE
  //   OUT_REG_CB
  //   REG_A1_WE
  //   REG_A2_WE
  //   REG_A3_WE
  //   REG_B1_WE
  //   REG_B2_WE
  //   REG_B3_WE
  //   SYSTEM_RAM_WE
  //   SYSTEM_RAM_OE
  //   RAM_B_OE
  //   CLOCK_RESET
  //   counter A
  //   counter B
  //   counter A increment
  //   counter B increment
  //   R0,R1,R2,R3 WE
  //   R0_CB
  //   R1_CB
  //   R2 _B
  //   R3_CB
  //   Program Counter CB
  //   Address A CB to MAR Z
  //   counter C
  //   Counter C increment
  //   Colck CB
  //   MAR A counter CB 
  //   MBR Z mid CB
  //   A0
  //   A1
  //   A2
  //   A3
  //   B0
  //   B1
  //   B2
  //   B3
  //   memory swap
  //   address b to mar z
  //   system ram CB
  //   Counter B CB
  //   Counter E we 
  //   Counter E increment
  //   C
  //   System__RAM
  //   RAM __B
  //   Step counter
  //   Opcode
  //   contents of rom_1 (hex, n*v repeats v):
  //   c0002000 30000000 c000000 43800000 0 1002 180000 78000 40004000 1 6*0 c0002000 30000000 c000000
  //   43800000 0 1002 180000 78000 40004000 1 6*0 c0002000 30000000 c000000 43800000 0 1002 180000 78000
  //   40004000 1 6*0 c0002000 30000000 c000000 43800000 0 1002 180000 78000 40004000 1 6*0 c0002000
  //   30000000 c000000 43800000 10000400 48020008 1 9*0 c0002000 30000000 c000000 43800000 0 1002 180000
  //   78000 40000000 1 6*0 c0002000 30000000 c000000 43800000 10000 200 100 80 8000 40 20 10 40000000 1 0
  //   0 c0002000 30000000 c000000 43800000 0 1002 181002 1f9002 1e1242 1e0120 40060090 1 4*0 c0002000
  //   30000000 c000000 43800000 0 10000000 18000008 18000008 18000008 48000008 1 5*0 c0002000 30000000
  //   c000000 43800000 0 1002 181002 1f9002 1e1242 1e0120 60090 40000000 1 0 0 0 c0002000 30000000 c000000
  //   43800000 0 1002 180000 78000 40004000 1 6*0 c0002000 30000000 c000000 43800000 0 1002 180000 78000
  //   40004000 1 6*0 c0002000 30000000 c000000 43800000 0 1002 180000 78000 40004000 1 6*0 c0002000
  //   30000000 c000000 43800000 0 1002 180000 78000 40004000 1 6*0 c0002000 30000000 c000000 43800000
  //   40000000 1 10*0 c0002000 30000000 c000000 43800000 40000000 0 80000004 50000004 50000004 50000004
  //   50000000 1 1
  //   First ROM
  //   contents of rom_2 (hex, n*v repeats v):
  //   400000 10000 0 200000 c0000000 20010 0 0 400000 7*0 400000 10000 0 200000 c0000000 20010 0 0 400000
  //   7*0 400000 10000 0 200000 c0000000 20010 0 0 400000 7*0 400000 10000 0 200000 c0000000 20010 0 0
  //   400000 7*0 400000 10000 0 200000 110000 400000 0 0 400000 7*0 400000 10000 0 200000 c0000000 20010 0
  //   0 420090 7*0 400000 10000 0 200000 8000 4000 2000 1000 800 400 200 100 400000 0 0 0 400000 10000 0
  //   200000 c0000000 30020010 30020010 30020010 20010 0 400000 5*0 400000 10000 0 200000 100000 4010000
  //   2090000 1090000 890000 400000 6*0 400000 10000 0 200000 c0000000 30020010 30020010 30020010 20010 0
  //   0 8400000 4*0 400000 10000 0 200000 c0000000 20010 0 0 400000 7*0 400000 10000 0 200000 c0000000
  //   20010 0 0 400000 7*0 400000 10000 0 200000 c0000000 20010 0 0 400000 7*0 400000 10000 0 200000
  //   c0000000 20010 0 0 400000 7*0 400000 10000 0 200000 440000 11*0 400000 10000 0 200000 40 100000
  //   c0000 8002a 80026 26 400026
  //   2nd ROM
endmodule

module InstSPILLTER (
  input  [15:0] Instruction,
  input  Write_Enable,
  input  clock,
  output [4:0] Add_B,
  output [4:0] Add_A,
  output [4:0] Opcode,
  output Flag,
  output NOP
);

  wire not_1_out;

  Register #(.width(16)) register_1 (
    .D(Instruction), .en(Write_Enable), .clk(clock), .Q({Flag, Opcode, Add_A, Add_B}));  // open: clr
  not not_1 (not_1_out, Opcode[0]);
  and and_1 (NOP, not_1_out, Opcode[1], Opcode[2], Opcode[3], Flag);
endmodule

module AND_operation (
  input  [15:0] A,
  input  [15:0] B,
  output [15:0] AND_result
);

  assign AND_result = A & B;  // AND_Gate and_1, 16 bits wide
endmodule

module XOR_opeation (
  input  [15:0] A,
  input  [15:0] B,
  output [15:0] XOR_result
);

  assign XOR_result = A ^ B;  // XOR_Gate xor_1, 16 bits wide
endmodule

module NOT_operation (
  input  [15:0] A,
  output [15:0] out_2
);

  assign out_2 = ~A;  // NOT_Gate not_1, 16 bits wide
endmodule

module try (
  input  [3:0] B,
  input  [3:0] A,
  output [7:0] Product
);

  wire [2:0] and_15_out;
  wire [3:0] and_4_out, and_8_out, and_12_out, fourbitadder_2_carryout;
  wire [3:1] fourbitadder_3_sum;
  wire [3:3] fourbitadder_3_carryout;

  // Probe on B
  and and_1 (and_4_out[3], B[3], A[3]);
  and and_2 (and_4_out[2], B[3], A[2]);
  and and_3 (and_4_out[1], B[3], A[1]);
  and and_4 (and_4_out[0], B[3], A[0]);
  and and_5 (and_8_out[3], B[2], A[3]);
  and and_6 (and_8_out[2], B[2], A[2]);
  and and_7 (and_8_out[1], B[2], A[1]);
  and and_8 (and_8_out[0], B[2], A[0]);
  and and_9 (and_12_out[3], B[1], A[3]);
  and and_10 (and_12_out[2], B[1], A[2]);
  and and_11 (and_12_out[1], B[1], A[1]);
  and and_12 (and_12_out[0], B[1], A[0]);
  FourBitAdder fourbitadder_1 (
    .CarryIn(1'b0), .A(fourbitadder_2_carryout), .B(and_4_out), .Sum(Product[6:3]), .CarryOut(Product[7]));
  FourBitAdder fourbitadder_2 (
    .CarryIn(1'b0), .A({fourbitadder_3_carryout[3], fourbitadder_3_sum}), .B(and_8_out),
    .Sum({fourbitadder_2_carryout[2:0], Product[2]}), .CarryOut(fourbitadder_2_carryout[3]));
  and and_13 (and_15_out[2], B[0], A[3]);
  and and_14 (and_15_out[1], B[0], A[2]);
  and and_15 (and_15_out[0], B[0], A[1]);
  FourBitAdder fourbitadder_3 (
    .CarryIn(1'b0), .A({1'b0, and_15_out}), .B(and_12_out), .Sum({fourbitadder_3_sum, Product[1]}),
    .CarryOut(fourbitadder_3_carryout[3]));
  // Probe on A
  and and_16 (Product[0], B[0], A[0]);
  // Probe on Product

  // Notes on the sheet:
  //   8 Bit Multiplier 
endmodule

module converter (
  input  [15:0] BInary,
  input  [15:0] Hex,
  input  [4:0] in_3,
  output [15:0] Hex_Binary,
  output [15:0] Bin,
  output [4:0] out_6
);

  // Probe on BInary
  // Probe on Hex

  assign Bin = Hex;
  assign Hex_Binary = BInary;
  assign out_6 = in_3;
endmodule

module MAt_mult (
  input  [15:0] A0,
  input  [15:0] A1,
  input  [15:0] A2,
  input  [15:0] A3,
  input  [15:0] B0,
  input  [15:0] B1,
  input  [15:0] B2,
  input  [15:0] B3,
  output [15:0] R0,
  output [15:0] R1,
  output [15:0] R2,
  output [15:0] R3
);

  wire [7:0] bitselector_1_out, bitselector_2_out, bitselector_3_out, bitselector_4_out, bitselector_5_out,
       bitselector_6_out, bitselector_7_out, bitselector_8_out;
  wire [15:0] eightbitmulti_1_product, eightbitmulti_2_product, eightbitmulti_3_product,
       eightbitmulti_4_product, eightbitmulti_5_product, eightbitmulti_6_product, eightbitmulti_7_product,
       eightbitmulti_8_product;

  BitSelector #(.group(8), .width(16)) bitselector_1 (.in(A0), .out(bitselector_1_out), .sel(1'b0));
  BitSelector #(.group(8), .width(16)) bitselector_2 (.in(A1), .out(bitselector_2_out), .sel(1'b0));
  BitSelector #(.group(8), .width(16)) bitselector_3 (.in(A2), .out(bitselector_3_out), .sel(1'b0));
  BitSelector #(.group(8), .width(16)) bitselector_4 (.in(A3), .out(bitselector_4_out), .sel(1'b0));
  BitSelector #(.group(8), .width(16)) bitselector_5 (.in(B0), .out(bitselector_5_out), .sel(1'b0));
  BitSelector #(.group(8), .width(16)) bitselector_6 (.in(B1), .out(bitselector_6_out), .sel(1'b0));
  BitSelector #(.group(8), .width(16)) bitselector_7 (.in(B2), .out(bitselector_7_out), .sel(1'b0));
  BitSelector #(.group(8), .width(16)) bitselector_8 (.in(B3), .out(bitselector_8_out), .sel(1'b0));
  EightBitMulti eightbitmulti_1 (
    .A(bitselector_1_out), .B(bitselector_5_out), .Product(eightbitmulti_1_product));  // open: C_out
  EightBitMulti eightbitmulti_2 (
    .A(bitselector_2_out), .B(bitselector_7_out), .Product(eightbitmulti_2_product));  // open: C_out
  EightBitMulti eightbitmulti_3 (
    .A(bitselector_1_out), .B(bitselector_6_out), .Product(eightbitmulti_3_product));  // open: C_out
  EightBitMulti eightbitmulti_4 (
    .A(bitselector_2_out), .B(bitselector_8_out), .Product(eightbitmulti_4_product));  // open: C_out
  EightBitMulti eightbitmulti_5 (
    .A(bitselector_3_out), .B(bitselector_5_out), .Product(eightbitmulti_5_product));  // open: C_out
  EightBitMulti eightbitmulti_6 (
    .A(bitselector_4_out), .B(bitselector_7_out), .Product(eightbitmulti_6_product));  // open: C_out
  EightBitMulti eightbitmulti_7 (
    .A(bitselector_3_out), .B(bitselector_6_out), .Product(eightbitmulti_7_product));  // open: C_out
  EightBitMulti eightbitmulti_8 (
    .A(bitselector_4_out), .B(bitselector_8_out), .Product(eightbitmulti_8_product));  // open: C_out
  SixteenBitAdder sixteenbitadder_1 (
    .A(eightbitmulti_1_product), .B(eightbitmulti_2_product), .Sum(R0));  // open: CarryIn, CarryOut
  SixteenBitAdder sixteenbitadder_2 (
    .A(eightbitmulti_3_product), .B(eightbitmulti_4_product), .Sum(R1));  // open: CarryIn, CarryOut
  SixteenBitAdder sixteenbitadder_3 (
    .A(eightbitmulti_5_product), .B(eightbitmulti_6_product), .Sum(R2));  // open: CarryIn, CarryOut
  SixteenBitAdder sixteenbitadder_4 (
    .A(eightbitmulti_7_product), .B(eightbitmulti_8_product), .Sum(R3));  // open: CarryIn, CarryOut

  // Notes on the sheet:
  //   "0" as constant because we want to select first 8 bits 
  //   A0
  //   A1
  //   A2
  //   A3
  //   B0
  //   *
  //   B2
  //   B1
  //   =
  //   B3
  //   A0B0
  //   +
  //   A2B0 
  //   +
  //   A1B2
  //   A0B1
  //   A3B2
  //   A2B1
  //   +
  //   A1B3
  //   A3B3
  //   +
  //   Matrix multiplication 
endmodule

module Com_1 (
  input  A,
  input  B,
  output A_EQUAL_B,
  output A_GREATER_B,
  output A_LESS_B
);

  wire and_1_out, and_2_out, not_1_out, not_2_out;

  not not_1 (not_1_out, A);
  not not_2 (not_2_out, B);
  and and_1 (and_1_out, not_1_out, not_2_out);
  and and_2 (and_2_out, A, B);
  and and_3 (A_GREATER_B, A, not_2_out);
  and and_4 (A_LESS_B, not_1_out, B);
  or or_1 (A_EQUAL_B, and_1_out, and_2_out);
endmodule

module Com_2 (
  input  [1:0] A,
  input  [1:0] B,
  output A_EQUAL_B,
  output A_GREATER_B,
  output A_LESS_B
);

  wire and_1_out, and_2_out, and_3_out, and_4_out, and_5_out, and_6_out, and_7_out, and_8_out, and_9_out,
       and_10_out, not_1_out, not_2_out, not_3_out, not_4_out;

  not not_1 (not_1_out, A[1]);
  not not_2 (not_2_out, A[0]);
  not not_3 (not_3_out, B[1]);
  not not_4 (not_4_out, B[0]);
  and and_1 (and_1_out, not_1_out, not_2_out, not_3_out, not_4_out);
  and and_2 (and_2_out, not_1_out, A[0], not_3_out, B[0]);
  and and_3 (and_3_out, A[1], not_2_out, B[1], not_4_out);
  and and_4 (and_4_out, A[1], A[0], B[1], B[0]);
  and and_5 (and_5_out, A[0], not_3_out, not_4_out);
  and and_6 (and_6_out, A[1], not_3_out);
  or or_1 (A_GREATER_B, and_5_out, and_6_out, and_7_out);
  and and_7 (and_7_out, A[1], A[0], not_4_out);
  and and_8 (and_8_out, not_1_out, not_2_out, B[0]);
  and and_9 (and_9_out, not_1_out, B[1]);
  or or_2 (A_LESS_B, and_8_out, and_9_out, and_10_out);
  and and_10 (and_10_out, not_2_out, B[1], B[0]);
  or or_3 (A_EQUAL_B, and_1_out, and_2_out, and_3_out, and_4_out);
endmodule

module Com_4 (
  input  [3:0] A,
  input  [3:0] B,
  output A_EQUAL_B,
  output A_GREATER_B,
  output A_LESS_B
);

  wire and_1_out, and_2_out, com_2_1_a_equal_b, com_2_1_a_greater_b, com_2_1_a_less_b, com_2_2_a_equal_b,
       com_2_2_a_greater_b, com_2_2_a_less_b;

  Com_2 com_2_1 (
    .A(A[1:0]), .B(B[1:0]), .A_EQUAL_B(com_2_1_a_equal_b), .A_GREATER_B(com_2_1_a_greater_b),
    .A_LESS_B(com_2_1_a_less_b));
  Com_2 com_2_2 (
    .A(A[3:2]), .B(B[3:2]), .A_EQUAL_B(com_2_2_a_equal_b), .A_GREATER_B(com_2_2_a_greater_b),
    .A_LESS_B(com_2_2_a_less_b));
  and and_1 (and_1_out, com_2_1_a_less_b, com_2_2_a_equal_b);
  and and_2 (and_2_out, com_2_1_a_greater_b, com_2_2_a_equal_b);
  and and_3 (A_EQUAL_B, com_2_1_a_equal_b, com_2_2_a_equal_b);
  or or_1 (A_GREATER_B, com_2_2_a_greater_b, and_2_out);
  or or_2 (A_LESS_B, and_1_out, com_2_2_a_less_b);
endmodule

module com_8 (
  input  [7:0] A,
  input  [7:0] B,
  output A_EQUAL_B,
  output A_GREATER_B,
  output A_LESS_B
);

  wire and_1_out, and_2_out, com_4_1_a_equal_b, com_4_1_a_greater_b, com_4_1_a_less_b, com_4_2_a_equal_b,
       com_4_2_a_greater_b, com_4_2_a_less_b;

  Com_4 com_4_1 (
    .A(A[3:0]), .B(B[3:0]), .A_EQUAL_B(com_4_1_a_equal_b), .A_GREATER_B(com_4_1_a_greater_b),
    .A_LESS_B(com_4_1_a_less_b));
  Com_4 com_4_2 (
    .A(A[7:4]), .B(B[7:4]), .A_EQUAL_B(com_4_2_a_equal_b), .A_GREATER_B(com_4_2_a_greater_b),
    .A_LESS_B(com_4_2_a_less_b));
  and and_1 (and_1_out, com_4_1_a_less_b, com_4_2_a_equal_b);
  and and_2 (and_2_out, com_4_1_a_greater_b, com_4_2_a_equal_b);
  and and_3 (A_EQUAL_B, com_4_1_a_equal_b, com_4_2_a_equal_b);
  or or_1 (A_GREATER_B, com_4_2_a_greater_b, and_2_out);
  or or_2 (A_LESS_B, and_1_out, com_4_2_a_less_b);
endmodule

module com_16 (
  input  [15:0] A,
  input  [15:0] B,
  output [15:0] Result
);

  wire and_1_out, and_2_out, and_3_out, com_8_1_a_equal_b, com_8_1_a_greater_b, com_8_1_a_less_b,
       com_8_2_a_equal_b, com_8_2_a_greater_b, com_8_2_a_less_b, or_1_out, or_2_out;
  wire [2:0] controlled_buffer_1_out;

  com_8 com_8_1 (
    .A(A[7:0]), .B(B[7:0]), .A_EQUAL_B(com_8_1_a_equal_b), .A_GREATER_B(com_8_1_a_greater_b),
    .A_LESS_B(com_8_1_a_less_b));
  com_8 com_8_2 (
    .A(A[15:8]), .B(B[15:8]), .A_EQUAL_B(com_8_2_a_equal_b), .A_GREATER_B(com_8_2_a_greater_b),
    .A_LESS_B(com_8_2_a_less_b));
  and and_1 (and_1_out, com_8_1_a_less_b, com_8_2_a_equal_b);
  and and_2 (and_2_out, com_8_1_a_greater_b, com_8_2_a_equal_b);
  and and_3 (and_3_out, com_8_1_a_equal_b, com_8_2_a_equal_b);
  or or_1 (or_1_out, com_8_2_a_greater_b, and_2_out);
  or or_2 (or_2_out, and_1_out, com_8_2_a_less_b);
  assign controlled_buffer_1_out = and_3_out ? 3'b010 : 3'bz;  // Controlled_Buffer controlled_buffer_1
  assign controlled_buffer_1_out = or_1_out ? 3'b100 : 3'bz;  // Controlled_Buffer controlled_buffer_2
  assign controlled_buffer_1_out = or_2_out ? 3'b001 : 3'bz;  // Controlled_Buffer controlled_buffer_3
  assign Result = {{13{1'b0}}, controlled_buffer_1_out};  // Bit_Extender bit_extender_1

  // Notes on the sheet:
  //   A = B
  //   A>B
  //   A<B
endmodule

module COm16bitNORmal (
  input  [15:0] A,
  input  [15:0] B,
  output Equal,
  output A_G_B,
  output B_G_A
);

  wire and_1_out, and_2_out, com_8_1_a_equal_b, com_8_1_a_greater_b, com_8_1_a_less_b, com_8_2_a_equal_b,
       com_8_2_a_greater_b, com_8_2_a_less_b;

  com_8 com_8_1 (
    .A(A[7:0]), .B(B[7:0]), .A_EQUAL_B(com_8_1_a_equal_b), .A_GREATER_B(com_8_1_a_greater_b),
    .A_LESS_B(com_8_1_a_less_b));
  com_8 com_8_2 (
    .A(A[15:8]), .B(B[15:8]), .A_EQUAL_B(com_8_2_a_equal_b), .A_GREATER_B(com_8_2_a_greater_b),
    .A_LESS_B(com_8_2_a_less_b));
  and and_1 (and_1_out, com_8_1_a_less_b, com_8_2_a_equal_b);
  and and_2 (and_2_out, com_8_1_a_greater_b, com_8_2_a_equal_b);
  and and_3 (Equal, com_8_1_a_equal_b, com_8_2_a_equal_b);
  or or_1 (A_G_B, com_8_2_a_greater_b, and_2_out);
  or or_2 (B_G_A, and_1_out, com_8_2_a_less_b);

  // Notes on the sheet:
  //   A = B
  //   A>B
  //   A<B
endmodule

module Bus_terminal_like_circuit (
  input  [4:0] Opcodee,
  input  [15:0] Data,
  input  [4:0] Address,
  input  Flag,
  output [4:0] Add_A,
  output [15:0] A_Value,
  output [4:0] Add_B,
  output [15:0] B_Value
);

  wire and_1_out, not_1_out;
  wire [4:0] controlled_buffer_3_out, controlled_buffer_4_out;
  wire [15:0] controlled_buffer_1_out, controlled_buffer_2_out;

  and and_1 (and_1_out, Opcodee[0], Opcodee[1], Opcodee[2], Opcodee[3]);
  not not_1 (not_1_out, Flag);
  assign controlled_buffer_1_out = not_1_out ? Data : 16'bz;  // Controlled_Buffer controlled_buffer_1
  assign controlled_buffer_2_out = Flag ? Data : 16'bz;  // Controlled_Buffer controlled_buffer_2
  assign controlled_buffer_3_out = not_1_out ? Address : 5'bz;  // Controlled_Buffer controlled_buffer_3
  assign controlled_buffer_4_out = Flag ? Address : 5'bz;  // Controlled_Buffer controlled_buffer_4
  assign Add_A = and_1_out ? controlled_buffer_3_out : 5'bz;  // Controlled_Buffer controlled_buffer_5
  assign A_Value = and_1_out ? controlled_buffer_1_out : 16'bz;  // Controlled_Buffer controlled_buffer_6
  assign Add_B = and_1_out ? controlled_buffer_4_out : 5'bz;  // Controlled_Buffer controlled_buffer_7
  assign B_Value = and_1_out ? controlled_buffer_2_out : 16'bz;  // Controlled_Buffer controlled_buffer_8
endmodule

module RAM_controler (
  input  [4:0] opcode,
  input  Flag,
  input  C,
  output A,
  output B
);

  wire com16bitnormal_1_equal, not_1_out;
  wire [15:0] bit_extender_1_out;

  assign bit_extender_1_out = {{11{1'b0}}, opcode};  // Bit_Extender bit_extender_1
  COm16bitNORmal com16bitnormal_1 (
    .A(bit_extender_1_out), .B(16'hf), .Equal(com16bitnormal_1_equal));  // open: A_G_B, B_G_A
  not not_1 (not_1_out, Flag);
  and and_1 (B, com16bitnormal_1_equal, Flag);
  and and_2 (A, com16bitnormal_1_equal, C, not_1_out);
endmodule

module Register_swap (
  input  [4:0] OPCODE,
  input  [15:0] RegA0,
  input  [15:0] RegA1,
  input  [15:0] RegA2,
  input  [15:0] RegA3,
  input  [15:0] RegB0,
  input  [15:0] RegB1,
  input  [15:0] RegB2,
  input  [15:0] RegB3,
  input  [4:0] Address_A,
  input  [4:0] Address_B,
  output [15:0] REG_B0,
  output [15:0] REG_B1,
  output [15:0] REG_B2,
  output [15:0] REG_B3,
  output [15:0] REG_A0,
  output [15:0] REG_A1,
  output [15:0] REG_A2,
  output [15:0] REG_A3
);

  wire and_1_out, and_2_out, and_3_out, and_4_out, and_5_out, and_6_out, and_7_out, and_8_out, and_9_out,
       not_1_out, not_2_out, not_3_out, not_4_out, not_5_out, not_6_out, not_7_out, not_8_out, not_9_out,
       not_10_out, not_11_out, not_12_out, not_13_out, not_14_out, not_15_out, not_16_out, not_17_out,
       not_18_out, not_19_out, not_20_out;
  wire [15:0] and_10_out, and_11_out, and_12_out, and_13_out, and_14_out, and_15_out, and_16_out, and_17_out,
       bit_extender_1_out, bit_extender_2_out, bit_extender_3_out, bit_extender_4_out, bit_extender_5_out,
       bit_extender_6_out, bit_extender_7_out, bit_extender_8_out, controlled_buffer_1_out,
       controlled_buffer_2_out, controlled_buffer_3_out, controlled_buffer_4_out, controlled_buffer_5_out,
       controlled_buffer_6_out, controlled_buffer_7_out, controlled_buffer_10_out, or_1_out, or_2_out;

  not not_1 (not_1_out, OPCODE[0]);
  not not_2 (not_2_out, OPCODE[3]);
  and and_1 (and_1_out, not_1_out, OPCODE[1], OPCODE[2], not_2_out);
  not not_3 (not_3_out, Address_A[0]);
  not not_4 (not_4_out, Address_A[1]);
  not not_5 (not_5_out, Address_A[2]);
  not not_6 (not_6_out, Address_A[3]);
  not not_7 (not_7_out, Address_A[4]);
  not not_8 (not_8_out, Address_B[0]);
  not not_9 (not_9_out, Address_B[1]);
  not not_10 (not_10_out, Address_B[2]);
  not not_11 (not_11_out, Address_B[3]);
  not not_12 (not_12_out, Address_B[4]);
  and and_2 (and_2_out, Address_A[0], not_4_out, not_5_out, not_6_out, not_7_out);
  and and_3 (and_3_out, not_3_out, Address_A[1], not_5_out, not_6_out, not_7_out);
  and and_4 (and_4_out, Address_A[0], Address_A[1], not_5_out, not_6_out, not_7_out);
  and and_5 (and_5_out, not_3_out, not_4_out, Address_A[2], not_6_out, not_7_out);
  and and_6 (and_6_out, Address_B[0], not_9_out, Address_B[2], not_11_out, not_12_out);
  and and_7 (and_7_out, not_8_out, Address_B[1], not_11_out, not_12_out, Address_B[2]);
  and and_8 (and_8_out, Address_B[0], Address_B[1], Address_B[2], not_11_out, not_12_out);
  and and_9 (and_9_out, not_8_out, not_9_out, not_10_out, Address_B[3], not_12_out);
  assign bit_extender_1_out = {{15{and_2_out}}, and_2_out};  // Bit_Extender bit_extender_1
  assign bit_extender_2_out = {{15{and_3_out}}, and_3_out};  // Bit_Extender bit_extender_2
  assign bit_extender_3_out = {{15{and_4_out}}, and_4_out};  // Bit_Extender bit_extender_3
  assign bit_extender_4_out = {{15{and_5_out}}, and_5_out};  // Bit_Extender bit_extender_4
  assign bit_extender_5_out = {{15{and_6_out}}, and_6_out};  // Bit_Extender bit_extender_5
  assign bit_extender_6_out = {{15{and_7_out}}, and_7_out};  // Bit_Extender bit_extender_6
  assign bit_extender_7_out = {{15{and_8_out}}, and_8_out};  // Bit_Extender bit_extender_7
  assign bit_extender_8_out = {{15{and_9_out}}, and_9_out};  // Bit_Extender bit_extender_8
  assign and_10_out = RegA0 & bit_extender_1_out;  // AND_Gate and_10, 16 bits wide
  assign and_11_out = RegA1 & bit_extender_2_out;  // AND_Gate and_11, 16 bits wide
  assign and_12_out = RegA2 & bit_extender_3_out;  // AND_Gate and_12, 16 bits wide
  assign and_13_out = RegA3 & bit_extender_4_out;  // AND_Gate and_13, 16 bits wide
  assign and_14_out = RegB0 & bit_extender_5_out;  // AND_Gate and_14, 16 bits wide
  assign and_15_out = RegB1 & bit_extender_6_out;  // AND_Gate and_15, 16 bits wide
  assign and_16_out = RegB2 & bit_extender_7_out;  // AND_Gate and_16, 16 bits wide
  assign and_17_out = RegB3 & bit_extender_8_out;  // AND_Gate and_17, 16 bits wide
  assign or_1_out = and_10_out | and_11_out | and_12_out | and_13_out;  // OR_Gate or_1, 16 bits wide
  assign or_2_out = and_14_out | and_15_out | and_16_out | and_17_out;  // OR_Gate or_2, 16 bits wide
  assign controlled_buffer_1_out = and_6_out ? or_1_out : 16'bz;  // Controlled_Buffer controlled_buffer_1
  assign controlled_buffer_2_out = and_7_out ? or_1_out : 16'bz;  // Controlled_Buffer controlled_buffer_2
  assign controlled_buffer_3_out = and_8_out ? or_1_out : 16'bz;  // Controlled_Buffer controlled_buffer_3
  assign controlled_buffer_4_out = and_9_out ? or_1_out : 16'bz;  // Controlled_Buffer controlled_buffer_4
  assign controlled_buffer_5_out = and_2_out ? or_2_out : 16'bz;  // Controlled_Buffer controlled_buffer_5
  assign controlled_buffer_6_out = and_3_out ? or_2_out : 16'bz;  // Controlled_Buffer controlled_buffer_6
  assign controlled_buffer_7_out = and_4_out ? or_2_out : 16'bz;  // Controlled_Buffer controlled_buffer_7
  assign controlled_buffer_6_out = not_18_out ? RegA1 : 16'bz;  // Controlled_Buffer controlled_buffer_8
  assign controlled_buffer_7_out = not_19_out ? RegA2 : 16'bz;  // Controlled_Buffer controlled_buffer_9
  assign controlled_buffer_10_out = not_20_out ? RegA3 : 16'bz;  // Controlled_Buffer controlled_buffer_10
  assign controlled_buffer_10_out = and_5_out ? or_2_out : 16'bz;  // Controlled_Buffer controlled_buffer_11
  assign controlled_buffer_3_out = not_15_out ? RegB2 : 16'bz;  // Controlled_Buffer controlled_buffer_12
  assign controlled_buffer_4_out = not_16_out ? RegB3 : 16'bz;  // Controlled_Buffer controlled_buffer_13
  assign controlled_buffer_5_out = not_17_out ? RegA0 : 16'bz;  // Controlled_Buffer controlled_buffer_14
  assign controlled_buffer_1_out = not_13_out ? RegB0 : 16'bz;  // Controlled_Buffer controlled_buffer_15
  assign controlled_buffer_2_out = not_14_out ? RegB1 : 16'bz;  // Controlled_Buffer controlled_buffer_16
  assign REG_B0 = and_1_out ? controlled_buffer_1_out : 16'bz;  // Controlled_Buffer controlled_buffer_17
  assign REG_B1 = and_1_out ? controlled_buffer_2_out : 16'bz;  // Controlled_Buffer controlled_buffer_18
  assign REG_B2 = and_1_out ? controlled_buffer_3_out : 16'bz;  // Controlled_Buffer controlled_buffer_19
  assign REG_B3 = and_1_out ? controlled_buffer_4_out : 16'bz;  // Controlled_Buffer controlled_buffer_20
  assign REG_A0 = and_1_out ? controlled_buffer_5_out : 16'bz;  // Controlled_Buffer controlled_buffer_21
  assign REG_A1 = and_1_out ? controlled_buffer_6_out : 16'bz;  // Controlled_Buffer controlled_buffer_22
  assign REG_A2 = and_1_out ? controlled_buffer_7_out : 16'bz;  // Controlled_Buffer controlled_buffer_23
  assign REG_A3 = and_1_out ? controlled_buffer_10_out : 16'bz;  // Controlled_Buffer controlled_buffer_24
  not not_13 (not_13_out, and_6_out);
  not not_14 (not_14_out, and_7_out);
  not not_15 (not_15_out, and_8_out);
  not not_16 (not_16_out, and_9_out);
  not not_17 (not_17_out, and_2_out);
  not not_18 (not_18_out, and_3_out);
  not not_19 (not_19_out, and_4_out);
  not not_20 (not_20_out, and_5_out);

  // Notes on the sheet:
  //   00001
  //   00010
  //   00011
  //   00100
  //   00101
  //   00111
  //   00110
  //   01000
endmodule
